# Fritzing sketch setup (saved by Fritzing 0.9.2b)
breadboards: 1

parts:
  R1 = Resistor [tolerance=±5% resistance=220 package=THT]
  Part1 = Arduino Uno (Rev3)
  J1 = Basic Servo
  IC1 = IC, DIP package, 8 pins [chip_label=IC]
  J2 = Basic Servo
  IC2 = IC, DIP package, 8 pins [chip_label=IC]

nets:
  N1: R1.Pin_0, Part1.A0
  N2: R1.Pin_1, Part1.5V, IC1.pin2, IC2.pin3
  N3: Part1.D9_PWM, IC1.pin1
  N4: Part1.D10_PWM/SS, IC2.pin4
  N5: Part1.GND, IC1.pin3, IC2.pin2
  N6: J1.vcc, IC1.pin7
  N7: J1.pulse, IC1.pin8
  N8: J2.gnd, IC2.pin7
  N9: J2.vcc, IC2.pin6
  N10: J2.pulse, IC2.pin5
